# Fritzing sketch electronic-scheme-1.0 (saved by Fritzing 0.9.4)
breadboards: 1

parts:
  part = Raspberry Pi Zero
  Teichpumpe = DC Motor
  Moisture01 = Soil Moisture Sensor
  Moisture02 = Soil Moisture Sensor
  Valve01 = Basic Servo
  Valve02 = Basic Servo
  ULN_2803_Darlington_Driver = Darlington Driver [package=dil18]

nets:
  5V: part.pin_2, part.pin_4, Moisture01.VCC, Moisture02.VCC, Valve01.vcc, Valve02.vcc
  GND: part.pin_6, part.pin_39, Moisture01.GND, Moisture02.GND, Valve01.gnd, Valve02.gnd, ULN_2803_Darlington_Driver.9
  N1: part.pin_13, Moisture01.SIG
  N2: part.pin_15, Moisture02.SIG
  N3: part.pin_18, ULN_2803_Darlington_Driver.1
  N4: part.pin_38, Valve01.pulse
  N5: part.pin_40, Valve02.pulse
  12V: Teichpumpe.pin_1
  N6: Teichpumpe.pin_2, ULN_2803_Darlington_Driver.18
